// Logisim project PBL_MIps_32Bit_Single_Cycle_Processor.circ as structural Verilog: 4 circuits, main circuit SINGLE_CYCLE
module SINGLE_CYCLE (
);

  wire alu_1_branch, and_1_out, CLOCK, control_unit_1_alusrc, control_unit_1_branch, control_unit_1_jump,
       control_unit_1_memread, control_unit_1_memtoreg, control_unit_1_memwrite, control_unit_1_regdst,
       control_unit_1_regwrite, RESET_2_out, RESET_3_out, RESET_out;
  wire [2:0] control_unit_1_alucontrol2_0;
  wire [4:0] multiplexer_3_out;
  wire [5:0] INS_5_0, Op;
  wire [15:0] bit_extender_1_out, bit_extender_4_out;
  wire [25:6] ram_1_data;
  wire [31:0] alu_1_out_5, INS_15_0, INS_25_0, multiplexer_1_out, multiplexer_2_out, multiplexer_4_out,
       multiplexer_5_out, n5bit_register_file_1_rd1, n5bit_register_file_1_rd2, n32_bit_adder_1_result, PC_q,
       ram_2_data, shift_left_1_result, shift_left_2_result;

  Clock clock_1 (.out(CLOCK));
  Counter #(.width(32), .max('hffffffff), .ongoal("stay")) PC (
    .load(1'b1), .D(multiplexer_4_out), .count(1'b0), .Q(PC_q), .clk(CLOCK), .clr(RESET_out));  // open: carry
  Button RESET (.out(RESET_out));
  Bit_Extender #(.in_width(32)) bit_extender_1 (.in(PC_q), .out(bit_extender_1_out));
  Button RESET_2 (.out(RESET_2_out));
  _32_bit_adder u_32_bit_adder_1 (.A(PC_q), .B(32'h1), .Result(n32_bit_adder_1_result));  // open: carry_out, overflow
  CONTROL_UNIT control_unit_1 (
    .Opcode(Op), .Jump(control_unit_1_jump), .RegDst(control_unit_1_regdst), .ALUSrc(control_unit_1_alusrc),
    .MemtoReg(control_unit_1_memtoreg), .RegWrite(control_unit_1_regwrite), .MemRead(control_unit_1_memread),
    .MemWrite(control_unit_1_memwrite), .Branch(control_unit_1_branch), .Funct(INS_5_0),
    .ALUControl2_0(control_unit_1_alucontrol2_0));
  RAM #(.addrWidth(16), .dataWidth(32)) ram_1 (
    .addr(bit_extender_1_out), .data({Op, ram_1_data, INS_5_0}), .sel(1'b1), .clk(CLOCK), .ld(1'b1),
    .clr(RESET_2_out));
  assign INS_15_0 = {{16{ram_1_data[15]}}, {ram_1_data[15:6], INS_5_0}};  // Bit_Extender bit_extender_2
  shift_left shift_left_1 (.A(INS_15_0), .B(32'h2), .Result(shift_left_1_result));
  _5BIT_REGISTER_FILE u_5bit_register_file_1 (
    .A1(ram_1_data[25:21]), .A2(ram_1_data[20:16]), .WD(multiplexer_5_out), .A3(multiplexer_3_out),
    .Write_EN(control_unit_1_regwrite), .RD1(n5bit_register_file_1_rd1), .RD2(n5bit_register_file_1_rd2),
    .CLK(CLOCK));
  Multiplexer #(.width(32), .enable("false")) multiplexer_1 (
    .in0(n32_bit_adder_1_result), .in1(shift_left_1_result), .out(multiplexer_1_out), .sel(and_1_out));
  and and_1 (and_1_out, control_unit_1_branch, alu_1_branch);
  Multiplexer #(.width(32), .enable("false")) multiplexer_2 (
    .in0(n5bit_register_file_1_rd2), .in1(INS_15_0), .out(multiplexer_2_out), .sel(control_unit_1_alusrc));
  ALU alu_1 (
    .Src_B(multiplexer_2_out), .Src_A(n5bit_register_file_1_rd1), .F(control_unit_1_alucontrol2_0),
    .out_5(alu_1_out_5), .Branch(alu_1_branch));
  Multiplexer #(.width(5), .enable("false")) multiplexer_3 (
    .in0(ram_1_data[20:16]), .in1(ram_1_data[15:11]), .out(multiplexer_3_out), .sel(control_unit_1_regdst));
  shift_left shift_left_2 (.A(INS_25_0), .B(32'h2), .Result(shift_left_2_result));
  assign INS_25_0 = {{6{ram_1_data[25]}}, {ram_1_data, INS_5_0}};  // Bit_Extender bit_extender_3
  Multiplexer #(.width(32), .enable("false")) multiplexer_4 (
    .in0(multiplexer_1_out), .in1(shift_left_2_result), .out(multiplexer_4_out), .sel(control_unit_1_jump));
  Bit_Extender #(.in_width(32)) bit_extender_4 (.in(alu_1_out_5), .out(bit_extender_4_out));
  Multiplexer #(.width(32), .enable("false")) multiplexer_5 (
    .in0(alu_1_out_5), .in1(ram_2_data), .out(multiplexer_5_out), .sel(control_unit_1_memtoreg));
  RAM #(.addrWidth(16), .dataWidth(32), .bus("separate")) ram_2 (
    .addr(bit_extender_4_out), .din(n5bit_register_file_1_rd2), .data(ram_2_data),
    .str(control_unit_1_memwrite), .sel(1'b1), .clk(CLOCK), .ld(control_unit_1_memread), .clr(RESET_3_out));
  Button RESET_3 (.out(RESET_3_out));

  // Notes on the sheet:
  //   Instruction Memory
  //   20:16
  //   25:21
  //   15:0
  //   WriteReg 4:0
  //   Write Data
  //   Data Memory
endmodule

module _5BIT_REGISTER_FILE (
  input  [4:0] A1,
  input  CLK,
  input  [4:0] A2,
  input  [31:0] WD,
  input  [4:0] A3,
  input  Write_EN,
  output [31:0] RD1,
  output [31:0] RD2
);

  wire demultiplexer_2_out0, demultiplexer_2_out1, demultiplexer_2_out2, demultiplexer_2_out3,
       demultiplexer_2_out4, demultiplexer_2_out5, demultiplexer_2_out6, demultiplexer_2_out7,
       demultiplexer_2_out8, demultiplexer_2_out9, demultiplexer_2_out10, demultiplexer_2_out11,
       demultiplexer_2_out12, demultiplexer_2_out13, demultiplexer_2_out14, demultiplexer_2_out15,
       demultiplexer_2_out16, demultiplexer_2_out17, demultiplexer_2_out18, demultiplexer_2_out19,
       demultiplexer_2_out20, demultiplexer_2_out21, demultiplexer_2_out22, demultiplexer_2_out23,
       demultiplexer_2_out24, demultiplexer_2_out25, demultiplexer_2_out26, demultiplexer_2_out27,
       demultiplexer_2_out28, demultiplexer_2_out29, demultiplexer_2_out30, demultiplexer_2_out31;
  wire [31:0] Address_00000_q, Address_00001_q, Address_00010_q, Address_00011_q, Address_00100_q,
       Address_00101_q, Address_00110_q, Address_00111_q, Address_01000_q, Address_01001_q, Address_01010_q,
       Address_01011_q, Address_01100_q, Address_01101_q, Address_01110_q, Address_01111_q, Address_10000_q,
       Address_10001_q, Address_10010_q, Address_10011_q, Address_10100_q, Address_10101_q, Address_10110_q,
       Address_10111_q, Address_11000_q, Address_11001_q, Address_11010_q, Address_11011_q, Address_11100_q,
       Address_11101_q, Address_11110_q, Address_11111_q, demultiplexer_1_out0, demultiplexer_1_out1,
       demultiplexer_1_out2, demultiplexer_1_out3, demultiplexer_1_out4, demultiplexer_1_out5,
       demultiplexer_1_out6, demultiplexer_1_out7, demultiplexer_1_out8, demultiplexer_1_out9,
       demultiplexer_1_out10, demultiplexer_1_out11, demultiplexer_1_out12, demultiplexer_1_out13,
       demultiplexer_1_out14, demultiplexer_1_out15, demultiplexer_1_out16, demultiplexer_1_out17,
       demultiplexer_1_out18, demultiplexer_1_out19, demultiplexer_1_out20, demultiplexer_1_out21,
       demultiplexer_1_out22, demultiplexer_1_out23, demultiplexer_1_out24, demultiplexer_1_out25,
       demultiplexer_1_out26, demultiplexer_1_out27, demultiplexer_1_out28, demultiplexer_1_out29,
       demultiplexer_1_out30, demultiplexer_1_out31;

  Demultiplexer #(.select(5), .width(32)) demultiplexer_1 (
    .out0(demultiplexer_1_out0), .out1(demultiplexer_1_out1), .out2(demultiplexer_1_out2),
    .out3(demultiplexer_1_out3), .out4(demultiplexer_1_out4), .out5(demultiplexer_1_out5),
    .out6(demultiplexer_1_out6), .out7(demultiplexer_1_out7), .out8(demultiplexer_1_out8),
    .out9(demultiplexer_1_out9), .out10(demultiplexer_1_out10), .out11(demultiplexer_1_out11),
    .out12(demultiplexer_1_out12), .out13(demultiplexer_1_out13), .out14(demultiplexer_1_out14),
    .out15(demultiplexer_1_out15), .out16(demultiplexer_1_out16), .out17(demultiplexer_1_out17),
    .out18(demultiplexer_1_out18), .out19(demultiplexer_1_out19), .out20(demultiplexer_1_out20),
    .out21(demultiplexer_1_out21), .out22(demultiplexer_1_out22), .out23(demultiplexer_1_out23),
    .out24(demultiplexer_1_out24), .out25(demultiplexer_1_out25), .out26(demultiplexer_1_out26),
    .out27(demultiplexer_1_out27), .out28(demultiplexer_1_out28), .out29(demultiplexer_1_out29),
    .out30(demultiplexer_1_out30), .out31(demultiplexer_1_out31), .in(WD), .sel(A3));  // open: en
  Demultiplexer #(.select(5)) demultiplexer_2 (
    .out0(demultiplexer_2_out0), .out1(demultiplexer_2_out1), .out2(demultiplexer_2_out2),
    .out3(demultiplexer_2_out3), .out4(demultiplexer_2_out4), .out5(demultiplexer_2_out5),
    .out6(demultiplexer_2_out6), .out7(demultiplexer_2_out7), .out8(demultiplexer_2_out8),
    .out9(demultiplexer_2_out9), .out10(demultiplexer_2_out10), .out11(demultiplexer_2_out11),
    .out12(demultiplexer_2_out12), .out13(demultiplexer_2_out13), .out14(demultiplexer_2_out14),
    .out15(demultiplexer_2_out15), .out16(demultiplexer_2_out16), .out17(demultiplexer_2_out17),
    .out18(demultiplexer_2_out18), .out19(demultiplexer_2_out19), .out20(demultiplexer_2_out20),
    .out21(demultiplexer_2_out21), .out22(demultiplexer_2_out22), .out23(demultiplexer_2_out23),
    .out24(demultiplexer_2_out24), .out25(demultiplexer_2_out25), .out26(demultiplexer_2_out26),
    .out27(demultiplexer_2_out27), .out28(demultiplexer_2_out28), .out29(demultiplexer_2_out29),
    .out30(demultiplexer_2_out30), .out31(demultiplexer_2_out31), .in(Write_EN), .sel(A3));  // open: en
  Register #(.width(32)) Address_00000 (
    .D(demultiplexer_1_out0), .en(demultiplexer_2_out0), .Q(Address_00000_q), .clk(CLK));  // open: clr
  Register #(.width(32)) Address_00001 (
    .D(demultiplexer_1_out1), .en(demultiplexer_2_out1), .Q(Address_00001_q), .clk(CLK));  // open: clr
  Register #(.width(32)) Address_00010 (
    .D(demultiplexer_1_out2), .en(demultiplexer_2_out2), .Q(Address_00010_q), .clk(CLK));  // open: clr
  Register #(.width(32)) Address_00011 (
    .D(demultiplexer_1_out3), .en(demultiplexer_2_out3), .Q(Address_00011_q), .clk(CLK));  // open: clr
  Register #(.width(32)) Address_00100 (
    .D(demultiplexer_1_out4), .en(demultiplexer_2_out4), .Q(Address_00100_q), .clk(CLK));  // open: clr
  Register #(.width(32)) Address_00101 (
    .D(demultiplexer_1_out5), .en(demultiplexer_2_out5), .Q(Address_00101_q), .clk(CLK));  // open: clr
  Register #(.width(32)) Address_00110 (
    .D(demultiplexer_1_out6), .en(demultiplexer_2_out6), .Q(Address_00110_q), .clk(CLK));  // open: clr
  Register #(.width(32)) Address_00111 (
    .D(demultiplexer_1_out7), .en(demultiplexer_2_out7), .Q(Address_00111_q), .clk(CLK));  // open: clr
  Register #(.width(32)) Address_01000 (
    .D(demultiplexer_1_out8), .en(demultiplexer_2_out8), .Q(Address_01000_q), .clk(CLK));  // open: clr
  Register #(.width(32)) Address_01001 (
    .D(demultiplexer_1_out9), .en(demultiplexer_2_out9), .Q(Address_01001_q), .clk(CLK));  // open: clr
  Register #(.width(32)) Address_01010 (
    .D(demultiplexer_1_out10), .en(demultiplexer_2_out10), .Q(Address_01010_q), .clk(CLK));  // open: clr
  Register #(.width(32)) Address_01011 (
    .D(demultiplexer_1_out11), .en(demultiplexer_2_out11), .Q(Address_01011_q), .clk(CLK));  // open: clr
  Register #(.width(32)) Address_01100 (
    .D(demultiplexer_1_out12), .en(demultiplexer_2_out12), .Q(Address_01100_q), .clk(CLK));  // open: clr
  Register #(.width(32)) Address_01101 (
    .D(demultiplexer_1_out13), .en(demultiplexer_2_out13), .Q(Address_01101_q), .clk(CLK));  // open: clr
  Register #(.width(32)) Address_01110 (
    .D(demultiplexer_1_out14), .en(demultiplexer_2_out14), .Q(Address_01110_q), .clk(CLK));  // open: clr
  Register #(.width(32)) Address_01111 (
    .D(demultiplexer_1_out15), .en(demultiplexer_2_out15), .Q(Address_01111_q), .clk(CLK));  // open: clr
  Register #(.width(32)) Address_10000 (
    .D(demultiplexer_1_out16), .en(demultiplexer_2_out16), .Q(Address_10000_q), .clk(CLK));  // open: clr
  Register #(.width(32)) Address_10001 (
    .D(demultiplexer_1_out17), .en(demultiplexer_2_out17), .Q(Address_10001_q), .clk(CLK));  // open: clr
  Register #(.width(32)) Address_10010 (
    .D(demultiplexer_1_out18), .en(demultiplexer_2_out18), .Q(Address_10010_q), .clk(CLK));  // open: clr
  Register #(.width(32)) Address_10011 (
    .D(demultiplexer_1_out19), .en(demultiplexer_2_out19), .Q(Address_10011_q), .clk(CLK));  // open: clr
  Register #(.width(32)) Address_10100 (
    .D(demultiplexer_1_out20), .en(demultiplexer_2_out20), .Q(Address_10100_q), .clk(CLK));  // open: clr
  Register #(.width(32)) Address_10101 (
    .D(demultiplexer_1_out21), .en(demultiplexer_2_out21), .Q(Address_10101_q), .clk(CLK));  // open: clr
  Register #(.width(32)) Address_10110 (
    .D(demultiplexer_1_out22), .en(demultiplexer_2_out22), .Q(Address_10110_q), .clk(CLK));  // open: clr
  Register #(.width(32)) Address_10111 (
    .D(demultiplexer_1_out23), .en(demultiplexer_2_out23), .Q(Address_10111_q), .clk(CLK));  // open: clr
  Register #(.width(32)) Address_11000 (
    .D(demultiplexer_1_out24), .en(demultiplexer_2_out24), .Q(Address_11000_q), .clk(CLK));  // open: clr
  Register #(.width(32)) Address_11001 (
    .D(demultiplexer_1_out25), .en(demultiplexer_2_out25), .Q(Address_11001_q), .clk(CLK));  // open: clr
  Register #(.width(32)) Address_11010 (
    .D(demultiplexer_1_out26), .en(demultiplexer_2_out26), .Q(Address_11010_q), .clk(CLK));  // open: clr
  Register #(.width(32)) Address_11011 (
    .D(demultiplexer_1_out27), .en(demultiplexer_2_out27), .Q(Address_11011_q), .clk(CLK));  // open: clr
  Register #(.width(32)) Address_11100 (
    .D(demultiplexer_1_out28), .en(demultiplexer_2_out28), .Q(Address_11100_q), .clk(CLK));  // open: clr
  Register #(.width(32)) Address_11101 (
    .D(demultiplexer_1_out29), .en(demultiplexer_2_out29), .Q(Address_11101_q), .clk(CLK));  // open: clr
  Register #(.width(32)) Address_11110 (
    .D(demultiplexer_1_out30), .en(demultiplexer_2_out30), .Q(Address_11110_q), .clk(CLK));  // open: clr
  Register #(.width(32)) Address_11111 (
    .D(demultiplexer_1_out31), .en(demultiplexer_2_out31), .Q(Address_11111_q), .clk(CLK));  // open: clr
  Multiplexer #(.select(5), .width(32)) multiplexer_1 (
    .in0(Address_00000_q), .in1(Address_00001_q), .in2(Address_00010_q), .in3(Address_00011_q),
    .in4(Address_00100_q), .in5(Address_00101_q), .in6(Address_00110_q), .in7(Address_00111_q),
    .in8(Address_01000_q), .in9(Address_01001_q), .in10(Address_01010_q), .in11(Address_01011_q),
    .in12(Address_01100_q), .in13(Address_01101_q), .in14(Address_01110_q), .in15(Address_01111_q),
    .in16(Address_10000_q), .in17(Address_10001_q), .in18(Address_10010_q), .in19(Address_10011_q),
    .in20(Address_10100_q), .in21(Address_10101_q), .in22(Address_10110_q), .in23(Address_10111_q),
    .in24(Address_11000_q), .in25(Address_11001_q), .in26(Address_11010_q), .in27(Address_11011_q),
    .in28(Address_11100_q), .in29(Address_11101_q), .in30(Address_11110_q), .in31(Address_11111_q),
    .out(RD1), .sel(A1));  // open: en
  Multiplexer #(.select(5), .width(32)) multiplexer_2 (
    .in0(Address_00000_q), .in1(Address_00001_q), .in2(Address_00010_q), .in3(Address_00011_q),
    .in4(Address_00100_q), .in5(Address_00101_q), .in6(Address_00110_q), .in7(Address_00111_q),
    .in8(Address_01000_q), .in9(Address_01001_q), .in10(Address_01010_q), .in11(Address_01011_q),
    .in12(Address_01100_q), .in13(Address_01101_q), .in14(Address_01110_q), .in15(Address_01111_q),
    .in16(Address_10000_q), .in17(Address_10001_q), .in18(Address_10010_q), .in19(Address_10011_q),
    .in20(Address_10100_q), .in21(Address_10101_q), .in22(Address_10110_q), .in23(Address_10111_q),
    .in24(Address_11000_q), .in25(Address_11001_q), .in26(Address_11010_q), .in27(Address_11011_q),
    .in28(Address_11100_q), .in29(Address_11101_q), .in30(Address_11110_q), .in31(Address_11111_q),
    .out(RD2), .sel(A2));  // open: en
endmodule

module ALU (
  input  [31:0] Src_B,
  input  [31:0] Src_A,
  input  [2:0] F,
  output Branch,
  output [31:0] out_5
);

  wire bit_extender_1_out, equal_1_result;
  wire [31:0] adder_1_out, and_1_out, bit_extender_2_out, multiplexer_1_out, n32_bit_subs_1_result,
       not_1_out, or_1_out;

  assign not_1_out = ~Src_B;  // NOT_Gate not_1, 32 bits wide
  _32_bit_subs u_32_bit_subs_1 (.A(Src_B), .B(Src_A), .Result(n32_bit_subs_1_result));  // open: carry_out, overflow
  Multiplexer #(.width(32)) multiplexer_1 (
    .in0(Src_B), .in1(not_1_out), .out(multiplexer_1_out), .sel(F[2]));  // open: en
  equal equal_1 (.A(n32_bit_subs_1_result), .B({32{1'b0}}), .Result(equal_1_result));
  assign and_1_out = multiplexer_1_out & Src_A;  // AND_Gate and_1, 32 bits wide
  assign or_1_out = multiplexer_1_out | Src_A;  // OR_Gate or_1, 32 bits wide
  Bit_Extender #(.in_width(3), .out_width(1)) bit_extender_1 (.in(F), .out(bit_extender_1_out));
  Adder #(.width(32)) adder_1 (.a(multiplexer_1_out), .b(Src_A), .out(adder_1_out), .cin(F[2]));  // open: cout
  Multiplexer multiplexer_2 (
    .in0(equal_1_result), .in1(equal_1_result), .out(Branch), .sel(bit_extender_1_out));  // open: en
  assign bit_extender_2_out = {{31{1'b0}}, adder_1_out[31]};  // Bit_Extender bit_extender_2
  Multiplexer #(.select(2), .width(32), .enable("false")) multiplexer_3 (
    .in0(and_1_out), .in1(or_1_out), .in2(adder_1_out), .in3(bit_extender_2_out), .out(out_5), .sel(F[1:0]));
endmodule

module CONTROL_UNIT (
  input  [5:0] Opcode,
  input  [5:0] Funct,
  output Jump,
  output RegDst,
  output ALUSrc,
  output MemtoReg,
  output RegWrite,
  output MemRead,
  output MemWrite,
  output Branch,
  output [2:0] ALUControl2_0
);

  wire Addi_out, and_1_out, or_1_out;

  and R_Type (RegDst, ~Opcode[5], ~Opcode[4], ~Opcode[3], ~Opcode[2], ~Opcode[1], ~Opcode[0]);  // AND_Gate
  and Addi (Addi_out, ~Opcode[5], ~Opcode[4], Opcode[3], ~Opcode[2], ~Opcode[1], ~Opcode[0]);  // AND_Gate
  or or_1 (or_1_out, Funct[3], Funct[0]);
  and LW (MemRead, Opcode[5], ~Opcode[4], ~Opcode[3], ~Opcode[2], Opcode[1], Opcode[0]);  // AND_Gate
  and and_1 (and_1_out, RegDst, Funct[1]);
  and and_2 (ALUControl2_0[0], RegDst, or_1_out);
  and SW (MemWrite, Opcode[5], ~Opcode[4], Opcode[3], ~Opcode[2], Opcode[1], Opcode[0]);  // AND_Gate
  or or_2 (ALUControl2_0[2], Branch, and_1_out);
  or or_3 (ALUControl2_0[1], ~RegDst, ~Funct[2]);  // OR_Gate
  and BEQ (Branch, ~Opcode[5], ~Opcode[4], ~Opcode[3], Opcode[2], ~Opcode[1], ~Opcode[0]);  // AND_Gate
  and J (Jump, ~Opcode[5], ~Opcode[4], ~Opcode[3], ~Opcode[2], Opcode[1], ~Opcode[0]);  // AND_Gate
  or or_4 (ALUSrc, MemRead, Addi_out, MemWrite);
  or or_5 (RegWrite, RegDst, Addi_out, MemRead);

  assign MemtoReg = MemRead;

  // Other names for the same wires on the sheet: ALUOp[1:0] = {RegDst, Branch}
endmodule
